// Logisim project da1_task1.circ as structural Verilog: 2 circuits, main circuit DUT
module DUT (
  input  [15:0] A,
  input  [15:0] B,
  output [15:0] DOUT,
  output AWON
);

  wire adder_15_cout, adder_16_cout, comparator_1_lt, nand_1_out, not_1_out, not_2_out, not_3_out;
  wire [1:0] adder_1_out, adder_2_out, adder_3_out, adder_4_out, adder_5_out, adder_6_out, adder_7_out,
       adder_8_out, adder_9_out, adder_10_out, adder_11_out, adder_12_out;
  wire [2:0] adder_13_out, adder_14_out;
  wire [2:2] adder_7_cout, adder_10_cout, adder_11_cout, adder_12_cout;
  wire [3:0] adder_15_out, adder_16_out;
  wire [3:3] adder_13_cout, adder_14_cout;

  Adder #(.width(1)) adder_1 (.a(A[11]), .b(A[12]), .out(adder_1_out[0]), .cin(A[10]), .cout(adder_1_out[1]));
  Adder #(.width(1)) adder_2 (.a(A[14]), .b(A[15]), .out(adder_2_out[0]), .cin(A[13]), .cout(adder_2_out[1]));
  Adder #(.width(1)) adder_3 (.a(B[11]), .b(B[12]), .out(adder_3_out[0]), .cin(B[10]), .cout(adder_3_out[1]));
  Adder #(.width(1)) adder_4 (.a(B[14]), .b(B[15]), .out(adder_4_out[0]), .cin(B[13]), .cout(adder_4_out[1]));
  Adder #(.width(1)) adder_5 (.a(A[4]), .b(A[5]), .out(adder_5_out[0]), .cin(A[3]), .cout(adder_5_out[1]));
  Adder #(.width(1)) adder_6 (.a(A[7]), .b(A[8]), .out(adder_6_out[0]), .cin(A[6]), .cout(adder_6_out[1]));
  Adder #(.width(2)) adder_7 (.a(adder_1_out), .b(adder_2_out), .out(adder_7_out), .cin(A[9]), .cout(adder_7_cout[2]));
  Adder #(.width(1)) adder_8 (.a(B[4]), .b(B[5]), .out(adder_8_out[0]), .cin(B[3]), .cout(adder_8_out[1]));
  Adder #(.width(1)) adder_9 (.a(B[7]), .b(B[8]), .out(adder_9_out[0]), .cin(B[6]), .cout(adder_9_out[1]));
  Adder #(.width(2)) adder_10 (
    .a(adder_3_out), .b(adder_4_out), .out(adder_10_out), .cin(B[9]), .cout(adder_10_cout[2]));
  Adder #(.width(2)) adder_11 (
    .a(adder_5_out), .b(adder_6_out), .out(adder_11_out), .cin(A[2]), .cout(adder_11_cout[2]));
  Adder #(.width(2)) adder_12 (
    .a(adder_8_out), .b(adder_9_out), .out(adder_12_out), .cin(B[2]), .cout(adder_12_cout[2]));
  Adder #(.width(3)) adder_13 (
    .a({adder_11_cout[2], adder_11_out}), .b({adder_7_cout[2], adder_7_out}), .out(adder_13_out), .cin(A[1]),
    .cout(adder_13_cout[3]));
  Adder #(.width(3)) adder_14 (
    .a({adder_12_cout[2], adder_12_out}), .b({adder_10_cout[2], adder_10_out}), .out(adder_14_out),
    .cin(B[1]), .cout(adder_14_cout[3]));
  Adder #(.width(4)) adder_15 (
    .a(4'b0000), .b({adder_13_cout[3], adder_13_out}), .out(adder_15_out), .cin(A[0]), .cout(adder_15_cout));
  Adder #(.width(4)) adder_16 (
    .a(4'b0000), .b({adder_14_cout[3], adder_14_out}), .out(adder_16_out), .cin(B[0]), .cout(adder_16_cout));
  not not_1 (not_1_out, comparator_1_lt);
  not not_2 (not_2_out, adder_16_cout);
  Comparator #(.mode("unsigned"), .width(4)) comparator_1 (
    .a(adder_15_out), .b(adder_16_out), .lt(comparator_1_lt));  // open: gt, eq
  not not_3 (not_3_out, adder_15_cout);
  nand nand_1 (nand_1_out, not_1_out, not_2_out);
  Multiplexer #(.width(16)) multiplexer_1 (.in0(B), .in1(A), .out(DOUT), .sel(AWON));
  nand nand_2 (AWON, not_3_out, nand_1_out);

  // Notes on the sheet:
  //   Please put your deisgn below. You may also use subcircuits.
  //   However, do not move or rename any pins.
endmodule

module TB (
  input  [15:0] A,
  input  [15:0] B,
  output [15:0] DOUT,
  output AWON
);

  DUT dut_1 (.A(A), .B(B), .DOUT(DOUT), .AWON(AWON));

  // Notes on the sheet:
  //   DO NOT MODIFY THIS
  //   TEST YOUR CIRCUITS USING THIS TO MAKE SURE YOU HAVE NOT ALTERED PIN OUT
endmodule
