// Logisim project da1_task2.circ as structural Verilog: 2 circuits, main circuit DUT
module DUT (
  input  [6:0] in_1,
  input  [6:0] in_2,
  input  [6:0] in_3,
  input  [6:0] in_4,
  input  [6:0] in_5,
  input  [6:0] SIGN,
  input  [6:0] D1,
  input  [6:0] D0,
  input  [6:0] in_9,
  input  [6:0] in_10,
  output [7:0] TC,
  output NAN
);

  wire nand_1_out, nand_2_out, nand_3_out, nand_4_out, nand_5_out, nand_6_out, nand_7_out, nand_8_out,
       nand_9_out, nand_10_out, nand_11_out, nand_12_out, nand_13_out, nand_14_out, nand_15_out, nand_16_out,
       nand_17_out, nand_18_out, nand_19_out, not_1_out, not_2_out, not_3_out, not_4_out, not_5_out,
       not_6_out, not_7_out, not_8_out, not_9_out, not_10_out, not_11_out, not_12_out, not_13_out,
       not_14_out, not_15_out, not_16_out, not_17_out, not_18_out, not_19_out, not_20_out, not_22_out,
       not_23_out, not_24_out, not_25_out, not_26_out, not_27_out;
  wire [6:0] adder_3_out, adder_4_out, adder_5_out, adder_6_out, d0_t, d1_t, multiplexer_1_out,
       multiplexer_2_out, multiplexer_3_out, multiplexer_4_out, multiplexer_5_out, not_21_out, uval;
  wire [7:0] bit_extender_1_out, not_28_out, not_29_out;

  Adder #(.width(7)) adder_1 (.a(D1), .b(in_10), .out(d1_t));  // open: cin, cout
  Adder #(.width(7)) adder_2 (.a(D0), .b(in_10), .out(d0_t));  // open: cin, cout
  not not_1 (not_1_out, d0_t[6]);
  not not_2 (not_2_out, d0_t[5]);
  not not_3 (not_3_out, d0_t[4]);
  not not_4 (not_4_out, d0_t[2]);
  not not_5 (not_5_out, d0_t[1]);
  not not_6 (not_6_out, d1_t[1]);
  not not_7 (not_7_out, d1_t[2]);
  not not_8 (not_8_out, d1_t[4]);
  not not_9 (not_9_out, d1_t[5]);
  not not_10 (not_10_out, d1_t[6]);
  not not_11 (not_11_out, SIGN[1]);
  not not_12 (not_12_out, SIGN[2]);
  not not_13 (not_13_out, SIGN[4]);
  not not_14 (not_14_out, SIGN[6]);
  nand nand_1 (nand_1_out, not_4_out, not_5_out);
  nand nand_2 (nand_2_out, not_6_out, not_7_out);
  Multiplexer #(.width(7)) multiplexer_1 (.in0(in_5), .in1(in_1), .out(multiplexer_1_out), .sel(d1_t[3]));
  Adder #(.width(7)) adder_3 (.a(multiplexer_1_out), .b(multiplexer_2_out), .out(adder_3_out));  // open: cin, cout
  Multiplexer #(.width(7)) multiplexer_2 (.in0(in_5), .in1(in_2), .out(multiplexer_2_out), .sel(d1_t[2]));
  Multiplexer #(.width(7)) multiplexer_3 (.in0(in_5), .in1(in_3), .out(multiplexer_3_out), .sel(d1_t[1]));
  Adder #(.width(7)) adder_4 (.a(multiplexer_3_out), .b(multiplexer_4_out), .out(adder_4_out));  // open: cin, cout
  Multiplexer #(.width(7)) multiplexer_4 (.in0(in_5), .in1(in_4), .out(multiplexer_4_out), .sel(d1_t[0]));
  nand nand_3 (nand_3_out, not_11_out, SIGN[2]);
  nand nand_4 (nand_4_out, SIGN[1], not_12_out);
  nand nand_5 (nand_5_out, SIGN[3], not_13_out);
  not not_15 (not_15_out, nand_5_out);
  nand nand_6 (nand_6_out, SIGN[5], not_14_out);
  not not_16 (not_16_out, nand_6_out);
  nand nand_7 (nand_7_out, not_1_out, not_2_out);
  not not_17 (not_17_out, nand_7_out);
  nand nand_8 (nand_8_out, not_3_out, nand_9_out);
  not not_18 (not_18_out, nand_8_out);
  nand nand_9 (nand_9_out, d0_t[3], nand_1_out);
  nand nand_10 (nand_10_out, nand_2_out, d1_t[3]);
  nand nand_11 (nand_11_out, nand_10_out, not_8_out);
  not not_19 (not_19_out, nand_11_out);
  nand nand_12 (nand_12_out, not_9_out, not_10_out);
  not not_20 (not_20_out, nand_12_out);
  Adder #(.width(7)) adder_5 (.a(adder_3_out), .b(adder_4_out), .out(adder_5_out));  // open: cin, cout
  assign not_21_out = ~uval;  // NOT_Gate not_21, 7 bits wide
  Adder #(.width(7)) adder_6 (.a(not_21_out), .b(in_9), .out(adder_6_out));  // open: cin, cout
  nand nand_13 (nand_13_out, SIGN[0], nand_14_out);
  nand nand_14 (nand_14_out, nand_3_out, nand_4_out);
  nand nand_15 (nand_15_out, not_15_out, not_16_out);
  not not_22 (not_22_out, nand_15_out);
  nand nand_16 (nand_16_out, not_17_out, not_18_out);
  not not_23 (not_23_out, nand_16_out);
  not not_24 (not_24_out, nand_17_out);
  nand nand_17 (nand_17_out, not_19_out, not_20_out);
  Adder #(.width(7)) adder_7 (.a(adder_5_out), .b(d0_t), .out(uval));  // open: cin, cout
  Multiplexer #(.width(7)) multiplexer_5 (.in0(uval), .in1(adder_6_out), .out(multiplexer_5_out), .sel(SIGN[2]));
  not not_25 (not_25_out, nand_13_out);
  nand nand_18 (nand_18_out, not_25_out, not_22_out);
  nand nand_19 (nand_19_out, not_23_out, not_24_out);
  not not_26 (not_26_out, nand_18_out);
  not not_27 (not_27_out, nand_19_out);
  assign not_28_out = ~{SIGN[2], multiplexer_5_out};  // NOT_Gate not_28, 8 bits wide
  assign not_29_out = ~bit_extender_1_out;  // NOT_Gate not_29, 8 bits wide
  assign bit_extender_1_out = {{7{NAN}}, NAN};  // Bit_Extender bit_extender_1
  nand nand_20 (NAN, not_26_out, not_27_out);
  assign TC = ~(not_28_out & not_29_out);  // NAND_Gate nand_21, 8 bits wide

  // Other names for the same wires on the sheet: sign_t = SIGN[2]

  // Notes on the sheet:
  //   in_10: initial=0x50
  //   in_3: initial=0x14
  //   in_4: initial=0xa
  //   in_1: initial=0x50
  //   in_2: initial=0x28
  //   in_9: initial=0x1
  //   Please put your deisgn below. You may also use subcircuits.
  //   However, do not move or rename any pins.
endmodule

module TB (
  input  [6:0] SIGN,
  input  [6:0] D1,
  input  [6:0] D0,
  output [7:0] DOUT,
  output NAN
);

  DUT dut_1 (.in_1(SIGN), .in_2(D1), .in_3(D0), .TC(DOUT), .NAN(NAN));  // open: in_4, in_5, SIGN, D1, D0, in_9, in_10

  // Notes on the sheet:
  //   DO NOT MODIFY THIS
  //   TEST YOUR CIRCUITS USING THIS TO MAKE SURE YOU HAVE NOT ALTERED PIN OUT
endmodule
