// Logisim project da1_task3.circ as structural Verilog: 3 circuits, main circuit DUT
module DUT (
  input  X,
  input  CLK,
  input  RST,
  output Z
);

  wire nand_1_out, nand_2_out, nand_3_out, nand_4_out, nand_5_out, nand_6_out, nand_7_out, nand_8_out,
       nand_9_out, nand_10_out, nand_11_out, nand_12_out, nand_13_out, nand_14_out, nand_15_out, nand_16_out,
       nand_17_out, nand_18_out, nand_19_out, nand_20_out, nand_21_out, nand_22_out, nand_23_out,
       nand_24_out, nand_25_out, nand_26_out, nand_27_out, nand_28_out, nand_29_out, nand_30_out,
       nand_31_out, nand_32_out, nand_33_out, nand_34_out, nand_35_out, nand_36_out, nand_37_out,
       nand_38_out, nand_39_out, nand_40_out, nand_47_out, nand_48_out, nand_49_out, nand_50_out,
       nand_51_out, nand_52_out, nand_53_out, nand_54_out, nand_55_out, nand_56_out, nand_57_out,
       nand_58_out, nand_59_out, nand_60_out, nand_61_out, not_1_out, not_2_out, not_3_out, not_4_out,
       not_5_out, not_6_out, not_7_out, not_8_out, not_9_out, not_10_out, not_11_out, t_ff_1_qn, t_ff_2_qn,
       t_ff_3_qn, t_ff_4_qn, t_ff_5_qn;
  wire [4:0] currstate, nextstate;

  not not_1 (not_1_out, X);
  not not_2 (not_2_out, currstate[4]);
  not not_3 (not_3_out, currstate[3]);
  not not_4 (not_4_out, currstate[2]);
  not not_5 (not_5_out, currstate[1]);
  not not_6 (not_6_out, currstate[0]);
  nand nand_1 (nand_1_out, not_2_out, not_3_out, not_4_out, not_5_out);
  nand nand_2 (nand_2_out, not_2_out, not_3_out, not_4_out, not_6_out);
  nand nand_3 (nand_3_out, X, not_2_out, not_4_out, not_5_out, currstate[0]);
  nand nand_4 (nand_4_out, currstate[3], not_4_out, currstate[1]);
  nand nand_5 (nand_5_out, currstate[3], currstate[2], not_5_out, not_6_out);
  nand nand_6 (nand_6_out, not_1_out, currstate[3], currstate[2], not_5_out);
  nand nand_7 (nand_7_out, not_1_out, currstate[3], currstate[1], not_6_out);
  nand nand_8 (nand_8_out, not_2_out, not_3_out, currstate[1], currstate[0]);
  nand nand_9 (nand_9_out, not_1_out, currstate[3], not_4_out, not_5_out);
  nand nand_10 (nand_10_out, X, currstate[2], currstate[1], not_6_out);
  nand nand_11 (nand_11_out, not_2_out, not_3_out, currstate[2]);
  nand nand_12 (nand_12_out, X, not_3_out, not_4_out, not_5_out, not_6_out);
  nand nand_13 (nand_13_out, not_1_out, not_3_out, currstate[2]);
  nand nand_14 (nand_14_out, X, not_2_out, not_3_out, currstate[1], not_6_out);
  nand nand_15 (nand_15_out, X, not_3_out, currstate[2], currstate[0]);
  nand nand_16 (nand_16_out, not_3_out, currstate[2], currstate[1]);
  nand nand_17 (nand_17_out, not_1_out, currstate[3], not_4_out, not_5_out);
  nand nand_18 (nand_18_out, X, currstate[3], currstate[2], not_6_out);
  nand nand_19 (nand_19_out, currstate[2], currstate[1], not_6_out);
  nand nand_20 (nand_20_out, X, currstate[2], currstate[1]);
  nand nand_21 (nand_21_out, not_1_out, currstate[4], not_4_out);
  nand nand_22 (nand_22_out, currstate[4], currstate[1], currstate[0]);
  nand nand_23 (nand_23_out, X, currstate[4], currstate[2]);
  nand nand_24 (nand_24_out, not_1_out, not_2_out, not_5_out, currstate[0]);
  nand nand_25 (nand_25_out, not_2_out, not_3_out, currstate[2], not_5_out, not_6_out);
  nand nand_26 (nand_26_out, not_1_out, currstate[3], not_5_out);
  nand nand_27 (nand_27_out, currstate[3], currstate[2], currstate[0]);
  nand nand_28 (nand_28_out, X, currstate[3], currstate[1]);
  nand nand_29 (nand_29_out, not_1_out, currstate[4], currstate[1]);
  nand nand_30 (nand_30_out, X, not_2_out, currstate[1], currstate[0]);
  nand nand_31 (nand_31_out, X, not_4_out, currstate[1], not_6_out);
  nand nand_32 (nand_32_out, not_2_out, not_3_out, not_4_out, not_5_out, not_6_out);
  nand nand_33 (nand_33_out, not_1_out, currstate[1], currstate[0]);
  nand nand_34 (nand_34_out, not_1_out, currstate[2], currstate[0]);
  nand nand_35 (nand_35_out, not_1_out, currstate[4], currstate[0]);
  nand nand_36 (nand_36_out, X, currstate[4], currstate[1], not_6_out);
  nand nand_37 (nand_37_out, X, not_3_out, currstate[2], not_6_out);
  nand nand_38 (nand_38_out, X, currstate[3], not_4_out, not_5_out);
  nand nand_39 (nand_39_out, currstate[3], not_4_out, currstate[0]);
  nand nand_40 (nand_40_out, X, currstate[3], currstate[2], currstate[1]);
  nand nand_41 (Z, nand_1_out, nand_2_out);
  nand nand_42 (nextstate[4], nand_3_out, nand_4_out, nand_5_out, nand_6_out, nand_7_out);
  nand nand_43 (nextstate[3], nand_8_out, nand_9_out, nand_10_out, nand_11_out, nand_12_out, nand_13_out);
  nand nand_44 (nextstate[2], nand_14_out, nand_15_out, nand_16_out, nand_17_out, nand_18_out, nand_19_out, nand_20_out, nand_21_out, nand_22_out, nand_23_out);
  nand nand_45 (nextstate[1], nand_24_out, nand_25_out, nand_26_out, nand_27_out, nand_28_out, nand_29_out, nand_30_out, nand_31_out);
  nand nand_46 (nextstate[0], nand_32_out, nand_33_out, nand_34_out, nand_35_out, nand_36_out, nand_37_out, nand_38_out, nand_39_out, nand_40_out);
  not not_7 (not_7_out, nextstate[0]);
  not not_8 (not_8_out, nextstate[1]);
  not not_9 (not_9_out, nextstate[2]);
  not not_10 (not_10_out, nextstate[3]);
  not not_11 (not_11_out, nextstate[4]);
  nand nand_47 (nand_47_out, currstate[0], not_7_out);
  T_Flip_Flop t_ff_1 (.T(nand_48_out), .clk(CLK), .Q(currstate[0]), .Qn(t_ff_1_qn), .reset(RST));  // open: preset
  nand nand_48 (nand_48_out, nand_47_out, nand_49_out);
  nand nand_49 (nand_49_out, t_ff_1_qn, nextstate[0]);
  nand nand_50 (nand_50_out, currstate[1], not_8_out);
  T_Flip_Flop t_ff_2 (.T(nand_51_out), .clk(CLK), .Q(currstate[1]), .Qn(t_ff_2_qn), .reset(RST));  // open: preset
  nand nand_51 (nand_51_out, nand_50_out, nand_52_out);
  nand nand_52 (nand_52_out, t_ff_2_qn, nextstate[1]);
  nand nand_53 (nand_53_out, currstate[2], not_9_out);
  T_Flip_Flop t_ff_3 (.T(nand_54_out), .clk(CLK), .Q(currstate[2]), .Qn(t_ff_3_qn), .reset(RST));  // open: preset
  nand nand_54 (nand_54_out, nand_53_out, nand_55_out);
  nand nand_55 (nand_55_out, t_ff_3_qn, nextstate[2]);
  nand nand_56 (nand_56_out, currstate[3], not_10_out);
  T_Flip_Flop t_ff_4 (.T(nand_57_out), .clk(CLK), .Q(currstate[3]), .Qn(t_ff_4_qn), .reset(RST));  // open: preset
  nand nand_57 (nand_57_out, nand_56_out, nand_58_out);
  nand nand_58 (nand_58_out, t_ff_4_qn, nextstate[3]);
  nand nand_59 (nand_59_out, currstate[4], not_11_out);
  T_Flip_Flop t_ff_5 (.T(nand_60_out), .clk(CLK), .Q(currstate[4]), .Qn(t_ff_5_qn), .reset(RST));  // open: preset
  nand nand_60 (nand_60_out, nand_59_out, nand_61_out);
  nand nand_61 (nand_61_out, t_ff_5_qn, nextstate[4]);

  // Other names for the same wires on the sheet: c = CLK; r = RST

  // Notes on the sheet:
  //   Please put your deisgn below. You may also use subcircuits.
  //   However, do not move, rename, add, or delete any pins.
endmodule

module TB (
);

  wire clk_out, mypor_1_p2, not_1_out, or_1_out, RESET_out, TimeIndex_carry, undriven;
  wire [0:0] dut_1_z;
  wire [4:0] TimeIndex_q;

  Clock #(.highDuration(2), .lowDuration(2)) clk (.out(clk_out));
  Clock sysclk ();  // open: out
  Counter #(.max('h1f), .ongoal("stay"), .width(5)) TimeIndex (
    .load(or_1_out), .clk(clk_out), .D({5{1'b0}}), .carry(TimeIndex_carry), .Q(TimeIndex_q));  // open: clr, up, count
  // MyPOR mypor_1: pin names not known; wires that end beside it: clk_out, mypor_1_p2
  Button RESET (.out(RESET_out));
  ROM #(.addrWidth(5), .dataWidth(1)) TestTraceMemory (.addr(TimeIndex_q));  // open: data
  or or_1 (or_1_out, mypor_1_p2, RESET_out);
  not not_1 (not_1_out, TimeIndex_carry);
  DUT dut_1 (.X(undriven), .CLK(clk_out), .RST(or_1_out), .Z(dut_1_z[0]));
  TTY tty_1 (.data({6'b011000, dut_1_z[0]}), .clk(clk_out), .we(not_1_out), .clr(or_1_out));
  LED DONE (.in(TimeIndex_carry));

  // Notes on the sheet:
  //   DO NOT MODIFY THIS
  //   YOU MAY TEST YOUR CIRCUITS USING THIS TO MAKE SURE YOU HAVE NOT ALTERED PIN OUT
  //   Edit ROM with input trace of 32 bits
endmodule

module TBRANDOM (
);

  wire clk_out, mypor_1_p2, not_1_out, or_1_out, random_1_out, RESET_out, TimeIndex_carry;
  wire [0:0] dut_1_z;

  Clock #(.highDuration(2), .lowDuration(2)) clk (.out(clk_out));
  Clock sysclk ();  // open: out
  Counter #(.ongoal("stay")) TimeIndex (
    .load(or_1_out), .clk(clk_out), .D({8{1'b0}}), .carry(TimeIndex_carry));  // open: clr, up, count, Q
  // MyPOR mypor_1: pin names not known; wires that end beside it: clk_out, mypor_1_p2
  Button RESET (.out(RESET_out));
  or or_1 (or_1_out, mypor_1_p2, RESET_out);
  Random #(.width(1)) random_1 (.clr(or_1_out), .clk(clk_out), .out(random_1_out));  // open: next
  not not_1 (not_1_out, TimeIndex_carry);
  DUT dut_1 (.X(random_1_out), .CLK(clk_out), .RST(or_1_out), .Z(dut_1_z[0]));
  TTY tty_1 (.data({6'b011000, dut_1_z[0]}), .clk(clk_out), .we(not_1_out), .clr(or_1_out));
  LED DONE (.in(TimeIndex_carry));

  // Notes on the sheet:
  //   DO NOT MODIFY THIS
  //   YOU MAY TEST YOUR CIRCUITS USING THIS TO MAKE SURE YOU HAVE NOT ALTERED PIN OUT
endmodule
