// Logisim project da1_task4.circ as structural Verilog: 2 circuits, main circuit DUT
module DUT (
  input  [15:0] DIN1,
  input  [15:0] DIN2,
  input  [15:0] DIN3,
  input  GO1,
  input  GO2,
  input  GO3,
  input  CLK,
  input  RST,
  output [15:0] DOUT,
  output DONE
);

  wire agtb, agtb1, agtb2, cltb, d_ff_1_qn, Great, Less, nagtb1, nagtb2, nand_1_out, nand_6_out, nand_7_out,
       nand_10_out, nand_11_out, nand_14_out, nand_16_out, nand_17_out, nand_19_out, nand_21_out,
       nand_23_out, ncltb, not_2_out, not_4_out, not_5_out, not_6_out, not_8_out, not_11_out, not_12_out,
       NRST, V1, V2, V3;
  wire [15:0] D1, D3, multiplexer_1_out;
  wire [16:0] bit_extender_1_out, bit_extender_2_out, bit_extender_3_out, bit_extender_4_out,
       bit_extender_5_out, bit_extender_6_out, bit_extender_7_out, bit_extender_8_out, bit_extender_9_out,
       nand_2_out, nand_3_out, nand_4_out, nand_5_out, nand_8_out, nand_9_out, nand_12_out, nand_13_out,
       nand_15_out, nand_18_out, nand_20_out, not_3_out, not_7_out, not_9_out, not_10_out;

  assign bit_extender_1_out = {{16{GO1}}, GO1};  // Bit_Extender bit_extender_1
  assign bit_extender_2_out = {{16{agtb}}, agtb};  // Bit_Extender bit_extender_2
  nand nand_1 (nand_1_out, agtb, Great);
  not not_1 (NRST, RST);
  assign bit_extender_3_out = {{16{NRST}}, NRST};  // Bit_Extender bit_extender_3
  assign nand_2_out = ~({1'b1, DIN1} & bit_extender_1_out);  // NAND_Gate nand_2, 17 bits wide
  assign nand_3_out = ~(bit_extender_2_out & {1'b0, DOUT});  // NAND_Gate nand_3, 17 bits wide
  not not_2 (not_2_out, GO1);
  assign nand_4_out = ~(bit_extender_3_out & nand_5_out);  // NAND_Gate nand_4, 17 bits wide
  assign nand_5_out = ~(nand_2_out & nand_3_out);  // NAND_Gate nand_5, 17 bits wide
  assign not_3_out = ~nand_4_out;  // NOT_Gate not_3, 17 bits wide
  Register #(.width(17)) register_1 (.D(not_3_out), .en(nand_6_out), .clk(CLK), .Q({V1, D1}));  // open: clr
  nand nand_6 (nand_6_out, nand_1_out, NRST, not_2_out);
  nand nand_7 (nand_7_out, nagtb1, ncltb, nagtb2, V1, V2, V3, NRST);
  assign bit_extender_4_out = {{16{GO2}}, GO2};  // Bit_Extender bit_extender_4
  assign bit_extender_5_out = {{16{agtb}}, agtb};  // Bit_Extender bit_extender_5
  assign nand_8_out = ~(bit_extender_5_out & {1'b0, D1});  // NAND_Gate nand_8, 17 bits wide
  assign bit_extender_6_out = {{16{cltb}}, cltb};  // Bit_Extender bit_extender_6
  assign nand_9_out = ~(bit_extender_6_out & {1'b0, D3});  // NAND_Gate nand_9, 17 bits wide
  nand nand_10 (nand_10_out, agtb, Great);
  not not_4 (not_4_out, GO2);
  nand nand_11 (nand_11_out, cltb, Less);
  D_Flip_Flop u_agtb1 (.D(not_5_out), .clk(CLK), .Q(agtb1), .Qn(nagtb1));  // open: preset, reset
  not not_5 (not_5_out, nand_7_out);
  assign bit_extender_7_out = {{16{NRST}}, NRST};  // Bit_Extender bit_extender_7
  assign nand_12_out = ~({1'b1, DIN2} & bit_extender_4_out);  // NAND_Gate nand_12, 17 bits wide
  assign nand_13_out = ~(nand_12_out & nand_8_out & nand_9_out);  // NAND_Gate nand_13, 17 bits wide
  D_Flip_Flop u_cltb (.D(not_6_out), .clk(CLK), .Q(cltb), .Qn(ncltb));  // open: preset, reset
  not not_6 (not_6_out, nand_14_out);
  nand nand_14 (nand_14_out, agtb1, NRST);
  assign nand_15_out = ~(bit_extender_7_out & nand_13_out);  // NAND_Gate nand_15, 17 bits wide
  assign not_7_out = ~nand_15_out;  // NOT_Gate not_7, 17 bits wide
  Register #(.width(17)) register_2 (.D(not_7_out), .en(nand_16_out), .clk(CLK), .Q({V2, DOUT}));  // open: clr
  nand nand_16 (nand_16_out, nand_10_out, NRST, not_4_out, nand_11_out);
  nand nand_17 (nand_17_out, ncltb, nagtb2);
  assign bit_extender_8_out = {{16{NRST}}, NRST};  // Bit_Extender bit_extender_8
  assign nand_18_out = ~({1'b1, DIN3} & bit_extender_9_out);  // NAND_Gate nand_18, 17 bits wide
  assign bit_extender_9_out = {{16{GO3}}, GO3};  // Bit_Extender bit_extender_9
  D_Flip_Flop u_agtb2 (.D(not_8_out), .clk(CLK), .Q(agtb2), .Qn(nagtb2));  // open: preset, reset
  nand nand_19 (nand_19_out, nand_17_out, NRST);
  not not_8 (not_8_out, nand_19_out);
  assign nand_20_out = ~(bit_extender_8_out & not_9_out);  // NAND_Gate nand_20, 17 bits wide
  assign not_9_out = ~nand_18_out;  // NOT_Gate not_9, 17 bits wide
  assign not_10_out = ~nand_20_out;  // NOT_Gate not_10, 17 bits wide
  nand nand_21 (nand_21_out, NRST, not_11_out);
  not not_11 (not_11_out, GO3);
  nand nand_22 (agtb, nagtb2, nagtb1);
  Register #(.width(17)) register_3 (.D(not_10_out), .en(nand_21_out), .clk(CLK), .Q({V3, D3}));  // open: clr
  D_Flip_Flop d_ff_1 (.D(not_12_out), .clk(CLK), .Q(DONE), .Qn(d_ff_1_qn));  // open: preset, reset
  nand nand_23 (nand_23_out, agtb2, NRST, d_ff_1_qn);
  not not_12 (not_12_out, nand_23_out);
  Multiplexer #(.width(16)) multiplexer_1 (.in0(D1), .in1(D3), .out(multiplexer_1_out), .sel(cltb));
  Comparator #(.width(16)) comparator_1 (.a(multiplexer_1_out), .b(DOUT), .gt(Great), .lt(Less));  // open: eq

  // Other names for the same wires on the sheet: D2[15:0] = DOUT

  // Notes on the sheet:
  //   Please put your design below. You may also use subcircuits.
  //   However, do not move, rename, add, or delete any pins.
endmodule

module TB (
  input  [15:0] DIN1,
  input  [15:0] DIN2,
  input  [15:0] DIN3,
  input  GO1,
  input  GO2,
  input  GO3,
  input  RST,
  output [15:0] DOUT,
  output DONE
);

  wire clk_out, or_1_out, RESET_out;

  Clock sysclk ();  // open: out
  Button RESET (.out(RESET_out));
  Clock #(.highDuration(2), .lowDuration(2)) clk (.out(clk_out));
  or or_1 (or_1_out, RESET_out, RST);
  DUT dut_1 (
    .DIN1(DIN1), .DIN2(DIN2), .DIN3(DIN3), .GO1(GO1), .GO2(GO2), .GO3(GO3), .CLK(clk_out), .RST(or_1_out),
    .DOUT(DOUT), .DONE(DONE));

  // Notes on the sheet:
  //   DO NOT MODIFY THIS
  //   YOU MAY TEST YOUR CIRCUITS USING THIS TO MAKE SURE YOU HAVE NOT ALTERED PIN OUT
endmodule
